// Logisim project q2_q.circ as structural Verilog: 3 circuits, main circuit main
module main (
  input  S0_2,
  input  S0_1,
  input  S0_0,
  output S_2,
  output S_1,
  output S_0
);

  wire and_1_out, and_2_out, and_3_out, and_4_out, and_5_out, and_6_out, and_7_out, and_8_out, not_2_out,
       not_3_out;

  not not_1 (S_0, S0_0);
  not not_2 (not_2_out, S0_2);
  not not_3 (not_3_out, S0_1);
  and and_1 (and_1_out, not_2_out, S0_1);
  and and_2 (and_2_out, S0_2, not_3_out);
  and and_3 (and_3_out, and_2_out, S_0);
  and and_4 (and_4_out, not_2_out, not_3_out);
  and and_5 (and_5_out, and_4_out, S0_0);
  and and_6 (and_6_out, not_2_out, S0_1);
  and and_7 (and_7_out, and_6_out, S_0);
  and and_8 (and_8_out, and_1_out, S0_0);
  or or_1 (S_2, and_8_out, and_3_out);
  or or_2 (S_1, and_5_out, and_7_out);
endmodule

module output_logic (
  input  S_2,
  input  S_1,
  input  S_0,
  output Output_2,
  output Output_1,
  output Output_0
);


  assign Output_0 = S_0;
  assign Output_1 = S_1;
  assign Output_2 = S_2;
endmodule

module TOTAL (
  output Output_2,
  output Output_1,
  output Output_0
);

  wire and_1_out, and_2_out, and_3_out, and_4_out, and_5_out, and_6_out, and_7_out, and_8_out, clock_1_out,
       not_1_out, not_2_out, not_3_out, or_1_out, or_2_out;

  not not_1 (not_1_out, Output_0);
  not not_2 (not_2_out, Output_1);
  not not_3 (not_3_out, Output_2);
  and and_1 (and_1_out, not_3_out, Output_1);
  and and_2 (and_2_out, Output_2, not_2_out);
  and and_3 (and_3_out, and_2_out, not_1_out);
  and and_4 (and_4_out, not_3_out, not_2_out);
  and and_5 (and_5_out, and_4_out, Output_0);
  and and_6 (and_6_out, not_3_out, Output_1);
  and and_7 (and_7_out, and_6_out, not_1_out);
  and and_8 (and_8_out, and_1_out, Output_0);
  or or_1 (or_1_out, and_8_out, and_3_out);
  or or_2 (or_2_out, and_5_out, and_7_out);
  Clock clock_1 (.out(clock_1_out));
  D_Flip_Flop d_ff_1 (.D(or_1_out), .clk(clock_1_out), .Q(Output_2));  // open: Qn, preset, reset
  D_Flip_Flop d_ff_2 (.D(or_2_out), .clk(clock_1_out), .Q(Output_1));  // open: Qn, preset, reset
  D_Flip_Flop d_ff_3 (.D(not_1_out), .clk(clock_1_out), .Q(Output_0));  // open: Qn, preset, reset
endmodule
