// Logisim project ex3.circ as structural Verilog: 3 circuits, main circuit rot1
module rot1 (
  input  [7:0] in_1,
  output [7:0] out_2
);


  assign out_2 = {in_1[0], in_1[7:1]};

  // Notes on the sheet:
  //   PUT CIRCUITRY HERE
endmodule

module Running_LED (
  input  [7:0] INITIAL_LED,
  input  RST,
  output [7:0] OUT_LED
);

  wire clock_1_out;
  wire [7:0] multiplexer_1_out, register_1_q;

  Clock clock_1 (.out(clock_1_out));
  LED led_1 (.in(OUT_LED[7]));
  Multiplexer #(.width(8)) multiplexer_1 (.in0(OUT_LED), .in1(INITIAL_LED), .out(multiplexer_1_out), .sel(RST));
  LED led_2 (.in(OUT_LED[6]));
  Register register_1 (.D(multiplexer_1_out), .clk(clock_1_out), .Q(register_1_q));  // open: en, clr
  LED led_3 (.in(OUT_LED[5]));
  rot1 rot1_1 (.in_1(register_1_q), .out_2(OUT_LED));
  LED led_4 (.in(OUT_LED[4]));
  LED led_5 (.in(OUT_LED[3]));
  LED led_6 (.in(OUT_LED[2]));
  LED led_7 (.in(OUT_LED[1]));
  LED led_8 (.in(OUT_LED[0]));

  // Notes on the sheet:
  //   PUT CIRCUITS HERE
endmodule

module new_running_LED (
  input  [7:0] INITIAL_LED,
  input  RST,
  input  [3:0] in_3,
  output [7:0] OUT_LED,
  output [3:0] out_5
);

  wire clock_1_out, comparator_1_lt;
  wire [3:0] multiplexer_2_out, register_2_q;
  wire [7:0] multiplexer_1_out, register_1_q, rot1_1_out_2;

  Clock clock_1 (.out(clock_1_out));
  LED led_1 (.in(OUT_LED[7]));
  Multiplexer #(.width(8)) multiplexer_1 (.in0(OUT_LED), .in1(INITIAL_LED), .out(multiplexer_1_out), .sel(RST));
  Multiplexer #(.width(4)) multiplexer_2 (.in0(out_5), .in1(in_3), .out(multiplexer_2_out), .sel(RST));
  LED led_2 (.in(OUT_LED[6]));
  Register register_1 (.D(multiplexer_1_out), .clk(clock_1_out), .Q(register_1_q));  // open: en, clr
  Register #(.width(4)) register_2 (.D(multiplexer_2_out), .clk(clock_1_out), .Q(register_2_q));  // open: en, clr
  LED led_3 (.in(OUT_LED[5]));
  rot1 rot1_1 (.in_1(register_1_q), .out_2(rot1_1_out_2));
  Adder #(.width(4)) adder_1 (.a(register_2_q), .b(4'b0001), .out(out_5));  // open: cin, cout
  Comparator #(.mode("unsigned"), .width(4)) comparator_1 (
    .a(out_5), .b(4'b1000), .lt(comparator_1_lt));  // open: gt, eq
  LED led_4 (.in(OUT_LED[4]));
  Multiplexer #(.width(8)) multiplexer_3 (.in1(rot1_1_out_2), .out(OUT_LED), .sel(comparator_1_lt));  // open: in0
  LED led_5 (.in(OUT_LED[3]));
  LED led_6 (.in(OUT_LED[2]));
  LED led_7 (.in(OUT_LED[1]));
  LED led_8 (.in(OUT_LED[0]));

  // Other names for the same wires on the sheet: INITIAL_COUNT[3:0] = in_3

  // Notes on the sheet:
  //   PUT CIRCUITS HERE
endmodule
