// Logisim project Lab8.circ as structural Verilog: 4 circuits, main circuit main
module main (
  output [7:0] non_pipe_out,
  output [7:0] pipe_out
);

  wire CLK_out, undriven;
  wire [7:0] Address_Counter_q, rom_1_data;

  Counter Address_Counter (.clk(CLK_out), .Q(Address_Counter_q));  // open: clr, load, up, count, D, carry
  Clock CLK (.out(CLK_out));
  ROM rom_1 (.addr(Address_Counter_q), .data(rom_1_data));
  // Probe on undriven
  non_pipelined non_pipelined_1 (
    .multiplicand(rom_1_data[3:0]), .in_2(rom_1_data[7:4]), .CLK(CLK_out), .product(non_pipe_out));
  pipelined pipelined_1 (
    .multiplicand(rom_1_data[3:0]), .multiplier(rom_1_data[7:4]), .CLK(CLK_out), .product(pipe_out));

  // Notes on the sheet:
  //   contents of rom_1 (hex, n*v repeats v):
  //   13 a2 fc 8f 1c 2 b0 d e 3 f 12 8 4 b 18 17 15 a 1a 11 c 19 9 10 a 1b 6 5 e 16 14 b 6 1c 1d 7 1 7 a
  //   1e f e 11 c 1f 9 d 14 2 13 8 10 18 15 7 16 1a 1b 17 19 3 5 d 9 12 1f 14 c b 4 1 e a d f 1d 18 1c 3 4
  //   17 16 12 11 b 13 14 2 1e 5 15 8 c 1a f 18 1b a 9 19 e 7 d 3 6 1c 17 4 10 12 b 8 f 16 1a 14 5 1 13 c
  //   e 2 1d 9 7 15 a 11 d 6 8 16 3 1f b 18 17 14 15 12 19 a 7 4 e c 2 1 13 f 6 9 d b 5 c 1a 1b a 1e 17 16
  //   14 11 19 18 15 b 7 3 8 f 1c 4 1d e 1a 12 9 2 5 10 6 1b 13 1 d a 1f 17 16 f 17 18 a 13 8 9 d b c 16 3
  //   1b 5 15 7 6 1d 10 2 1 e 4 c 1f 11 e 14 1c a 1a 9 12 b 8 d f 3 7 6 1e 19 1d c 15 16 a 5 2 13 b f 1f 4
  //   1c 9 7 8 15 10 1a 12 d 6
endmodule

module non_pipelined (
  input  [3:0] multiplicand,
  input  [3:0] in_2,
  input  CLK,
  output [7:0] product
);

  wire [7:0] shift_and_add_1_partial_product, shift_and_add_1_shifted_multiplicand,
       shift_and_add_2_partial_product, shift_and_add_2_shifted_multiplicand,
       shift_and_add_3_partial_product, shift_and_add_3_shifted_multiplicand, shift_and_add_4_partial_product;

  shift_and_add shift_and_add_1 (
    .current_sum({8{1'b0}}), .multiplicand({4'b0000, multiplicand}), .multiplier(in_2[0]),
    .partial_product(shift_and_add_1_partial_product),
    .shifted_multiplicand(shift_and_add_1_shifted_multiplicand));
  shift_and_add shift_and_add_2 (
    .current_sum(shift_and_add_1_partial_product), .multiplicand(shift_and_add_1_shifted_multiplicand),
    .multiplier(in_2[1]), .partial_product(shift_and_add_2_partial_product),
    .shifted_multiplicand(shift_and_add_2_shifted_multiplicand));
  shift_and_add shift_and_add_3 (
    .current_sum(shift_and_add_2_partial_product), .multiplicand(shift_and_add_2_shifted_multiplicand),
    .multiplier(in_2[2]), .partial_product(shift_and_add_3_partial_product),
    .shifted_multiplicand(shift_and_add_3_shifted_multiplicand));
  shift_and_add shift_and_add_4 (
    .current_sum(shift_and_add_3_partial_product), .multiplicand(shift_and_add_3_shifted_multiplicand),
    .multiplier(in_2[3]), .partial_product(shift_and_add_4_partial_product));  // open: shifted_multiplicand
  Register register_1 (.D(shift_and_add_4_partial_product), .clk(CLK), .Q(product));  // open: en, clr
endmodule

module pipelined (
  input  [3:0] multiplicand,
  input  [3:0] multiplier,
  input  CLK,
  output [7:0] product
);

  wire adder_1_cout, adder_2_cout, adder_2_out, adder_3_cout, adder_3_out, adder_4_cout, adder_4_out,
       adder_5_cout, adder_5_out, adder_6_cout, adder_6_out, adder_7_cout, adder_8_cout, adder_9_cout,
       adder_10_cout;
  wire [3:0] multiplexer_1_out, multiplexer_5_out, multiplexer_9_out, multiplexer_13_out, register_2_q,
       register_3_q, register_4_q;
  wire [3:1] register_1_q;

  Multiplexer multiplexer_1 (.in0(1'b0), .in1(multiplier[0]), .out(multiplexer_1_out[0]), .sel(multiplicand[0]));
  Multiplexer multiplexer_2 (.in0(1'b0), .in1(multiplier[1]), .out(multiplexer_1_out[1]), .sel(multiplicand[0]));
  Multiplexer multiplexer_3 (.in0(1'b0), .in1(multiplier[2]), .out(multiplexer_1_out[2]), .sel(multiplicand[0]));
  Multiplexer multiplexer_4 (.in0(1'b0), .in1(multiplier[3]), .out(multiplexer_1_out[3]), .sel(multiplicand[0]));
  Register #(.width(4)) register_1 (.D(multiplexer_1_out), .clk(CLK), .Q({register_1_q, product[0]}));  // open: en, clr
  Multiplexer multiplexer_5 (.in0(1'b0), .in1(multiplier[0]), .out(multiplexer_5_out[0]), .sel(multiplicand[1]));
  Multiplexer multiplexer_6 (.in0(1'b0), .in1(multiplier[1]), .out(multiplexer_5_out[1]), .sel(multiplicand[1]));
  Multiplexer multiplexer_7 (.in0(1'b0), .in1(multiplier[2]), .out(multiplexer_5_out[2]), .sel(multiplicand[1]));
  Multiplexer multiplexer_8 (.in0(1'b0), .in1(multiplier[3]), .out(multiplexer_5_out[3]), .sel(multiplicand[1]));
  Multiplexer multiplexer_9 (.in0(1'b0), .in1(multiplier[0]), .out(multiplexer_9_out[0]), .sel(multiplicand[2]));
  Multiplexer multiplexer_10 (.in0(1'b0), .in1(multiplier[1]), .out(multiplexer_9_out[1]), .sel(multiplicand[2]));
  Multiplexer multiplexer_11 (.in0(1'b0), .in1(multiplier[2]), .out(multiplexer_9_out[2]), .sel(multiplicand[2]));
  Multiplexer multiplexer_12 (.in0(1'b0), .in1(multiplier[3]), .out(multiplexer_9_out[3]), .sel(multiplicand[2]));
  Register #(.width(4)) register_2 (.D(multiplexer_5_out), .clk(CLK), .Q(register_2_q));  // open: en, clr
  Register #(.width(4)) register_3 (.D(multiplexer_9_out), .clk(CLK), .Q(register_3_q));  // open: en, clr
  Multiplexer multiplexer_13 (.in0(1'b0), .in1(multiplier[0]), .out(multiplexer_13_out[0]), .sel(multiplicand[3]));
  Multiplexer multiplexer_14 (.in0(1'b0), .in1(multiplier[1]), .out(multiplexer_13_out[1]), .sel(multiplicand[3]));
  Multiplexer multiplexer_15 (.in0(1'b0), .in1(multiplier[2]), .out(multiplexer_13_out[2]), .sel(multiplicand[3]));
  Multiplexer multiplexer_16 (.in0(1'b0), .in1(multiplier[3]), .out(multiplexer_13_out[3]), .sel(multiplicand[3]));
  Register #(.width(4)) register_4 (.D(multiplexer_13_out), .clk(CLK), .Q(register_4_q));  // open: en, clr
  Adder #(.width(1)) adder_1 (
    .a(register_1_q[1]), .b(register_2_q[0]), .out(product[1]), .cout(adder_1_cout));  // open: cin
  Adder #(.width(1)) adder_2 (
    .a(register_2_q[1]), .b(register_3_q[0]), .out(adder_2_out), .cin(register_1_q[2]), .cout(adder_2_cout));
  Adder #(.width(1)) adder_3 (
    .a(register_2_q[2]), .b(register_3_q[1]), .out(adder_3_out), .cin(register_1_q[3]), .cout(adder_3_cout));
  Adder #(.width(1)) adder_4 (
    .a(adder_3_out), .b(register_4_q[0]), .out(adder_4_out), .cin(adder_3_cout), .cout(adder_4_cout));
  Adder #(.width(1)) adder_5 (
    .a(register_2_q[3]), .b(register_4_q[1]), .out(adder_5_out), .cin(register_3_q[2]), .cout(adder_5_cout));
  Adder #(.width(1)) adder_6 (
    .a(register_3_q[3]), .b(register_4_q[2]), .out(adder_6_out), .cout(adder_6_cout));  // open: cin
  Adder #(.width(1)) adder_7 (.a(adder_1_cout), .b(adder_2_out), .out(product[2]), .cout(adder_7_cout));  // open: cin
  Adder #(.width(1)) adder_8 (
    .a(adder_2_cout), .b(adder_4_out), .out(product[3]), .cin(adder_7_cout), .cout(adder_8_cout));
  Adder #(.width(1)) adder_9 (
    .a(adder_4_cout), .b(adder_5_out), .out(product[4]), .cin(adder_8_cout), .cout(adder_9_cout));
  Adder #(.width(1)) adder_10 (
    .a(adder_5_cout), .b(adder_6_out), .out(product[5]), .cin(adder_9_cout), .cout(adder_10_cout));
  Adder #(.width(1)) adder_11 (
    .a(adder_6_cout), .b(register_4_q[3]), .out(product[6]), .cin(adder_10_cout), .cout(product[7]));
endmodule

module shift_and_add (
  input  [7:0] current_sum,
  input  [7:0] multiplicand,
  input  multiplier,
  output [7:0] partial_product,
  output [7:0] shifted_multiplicand
);

  wire [7:0] multiplexer_1_out;

  Multiplexer #(.enable("true"), .width(8)) multiplexer_1 (
    .in0({8{1'b0}}), .in1(multiplicand), .out(multiplexer_1_out), .sel(multiplier));  // open: en
  Adder adder_1 (.a(current_sum), .b(multiplexer_1_out), .out(partial_product));  // open: cin, cout
  Shifter shifter_1 (.in(multiplicand), .\dist (3'b001), .out(shifted_multiplicand));
endmodule
