// Logisim project proj_2_1.circ as structural Verilog: 13 circuits, main circuit testbench
module inst_fetch (
  input  clk,
  input  rst,
  input  control_en_i,
  input  [31:0] control_pc_i,
  input  [15:0] inst_i,
  output inst_en_o,
  output [31:0] current_pc_o,
  output [31:0] inst_addr_o,
  output [15:0] inst_o
);

  wire not_1_out, not_2_out;
  wire [31:0] adder_1_out, counter_1_q, multiplexer_1_out;

  not not_1 (not_1_out, rst);
  Adder #(.width(32)) adder_1 (.a(control_pc_i), .b(32'h1), .out(adder_1_out));  // open: cin, cout
  Counter #(.max('hffffffff), .width(32)) counter_1 (
    .clr(rst), .load(control_en_i), .up(not_1_out), .count(not_1_out), .clk(clk), .D(adder_1_out),
    .Q(counter_1_q));  // open: carry
  Multiplexer #(.width(32)) multiplexer_1 (
    .in0(counter_1_q), .in1(control_pc_i), .out(multiplexer_1_out), .sel(control_en_i));
  not not_2 (not_2_out, rst);
  Register #(.width(32)) register_1 (.D(multiplexer_1_out), .en(not_2_out), .clk(clk), .Q(current_pc_o), .clr(rst));
  not not_3 (inst_en_o, rst);

  assign inst_addr_o = current_pc_o;
  assign inst_o = inst_i;

  // Notes on the sheet:
  //   Don't touch
endmodule

module TOP (
  input  rst,
  input  clk,
  input  [15:0] inst,
  input  [31:0] mem_result,
  input  [31:0] current_pc,
  output mem_wen,
  output [31:0] mem_din,
  output mem_ren,
  output [31:0] alu_result,
  output control_en,
  output [31:0] control_pc,
  output wb_en,
  output [4:0] wb_addr,
  output [31:0] wb_data
);

  wire add, addi, addi4spn, beqz, control_en_1, halt, instruc_add_1_control_en, instruc_add_1_mem_ren,
       instruc_add_1_mem_wen, instruc_add_1_wb_en, instruc_addi_1_control_en, instruc_addi_1_mem_ren,
       instruc_addi_1_mem_wen, instruc_addi_1_wb_en, instruc_li_1_control_en, instruc_li_1_mem_ren,
       instruc_li_1_mem_wen, instruc_li_1_wb_en, instruc_lui_1_control_en, instruc_lui_1_mem_ren,
       instruc_lui_1_mem_wen, instruc_lui_1_wb_en, instruc_mv_1_control_en, instruc_mv_1_mem_ren,
       instruc_mv_1_mem_wen, instruc_mv_1_wb_en, instruc_slli_1_control_en, instruc_slli_1_mem_ren,
       instruc_slli_1_mem_wen, instruc_slli_1_wb_en, j, li, lui, lw, mem_ren_1, mem_wen_1, mv, register_1_q,
       register_2_q, register_3_q, register_4_q, slli, sw, swsp, wb_en_1;
  wire [4:0] instruc_add_1_rd, instruc_addi_1_rd, instruc_li_1_rd, instruc_lui_1_rd, instruc_mv_1_rd,
       instruc_slli_1_rd, register_5_q, wb_addr_1;
  wire [31:0] alu_result_1, control_pc_1, instruc_add_1_alu_result, instruc_add_1_wb_data,
       instruc_addi_1_alu_result, instruc_addi_1_wb_data, instruc_li_1_alu_result, instruc_li_1_wb_data,
       instruc_lui_1_alu_result, instruc_lui_1_wb_data, instruc_mv_1_alu_result, instruc_mv_1_wb_data,
       instruc_slli_1_alu_result, instruc_slli_1_wb_data, mem_din_1, register_6_q, register_7_q,
       register_8_q, wb_data_1, x_rs1, x_rs2;

  instruc_li instruc_li_1 (
    .clk(clk), .part3(inst[9:7]), .part4(inst[11:10]), .part5(inst[12]), .part1(inst[4:2]),
    .part2(inst[6:5]), .mem_wen(instruc_li_1_mem_wen), .mem_ren(instruc_li_1_mem_ren),
    .control_en(instruc_li_1_control_en), .wb_en(instruc_li_1_wb_en), .rd(instruc_li_1_rd),
    .wb_data(instruc_li_1_wb_data), .alu_result(instruc_li_1_alu_result));
  instruc_lui instruc_lui_1 (
    .clk(clk), .part3(inst[9:7]), .part4(inst[11:10]), .part5(inst[12]), .part1(inst[4:2]),
    .part2(inst[6:5]), .mem_wen(instruc_lui_1_mem_wen), .mem_ren(instruc_lui_1_mem_ren),
    .control_en(instruc_lui_1_control_en), .wb_en(instruc_lui_1_wb_en), .rd(instruc_lui_1_rd),
    .wb_data(instruc_lui_1_wb_data), .alu_result(instruc_lui_1_alu_result));
  Multiplexer multiplexer_1 (.in1(instruc_li_1_mem_wen), .out(mem_wen_1), .sel(li));  // open: in0
  Multiplexer multiplexer_2 (.in1(instruc_li_1_control_en), .out(control_en_1), .sel(li));  // open: in0
  Multiplexer #(.width(32)) multiplexer_3 (.in1(instruc_li_1_wb_data), .out(wb_data_1), .sel(li));  // open: in0
  Multiplexer multiplexer_4 (.in1(instruc_lui_1_mem_wen), .out(mem_wen_1), .sel(lui));  // open: in0
  Multiplexer multiplexer_5 (.in1(instruc_lui_1_control_en), .out(control_en_1), .sel(lui));  // open: in0
  Multiplexer #(.width(32)) multiplexer_6 (.in1(instruc_lui_1_wb_data), .out(wb_data_1), .sel(lui));  // open: in0
  Multiplexer multiplexer_7 (.in1(1'b0), .out(mem_wen_1), .sel(halt));  // open: in0
  Multiplexer #(.width(32)) multiplexer_8 (.in1({32{1'b0}}), .out(mem_din_1), .sel(halt));  // open: in0
  Multiplexer multiplexer_9 (.in1(1'b0), .out(mem_ren_1), .sel(halt));  // open: in0
  Multiplexer #(.width(32)) multiplexer_10 (.in1({32{1'b0}}), .out(alu_result_1), .sel(halt));  // open: in0
  Multiplexer multiplexer_11 (.in1(1'b0), .out(control_en_1), .sel(halt));  // open: in0
  Multiplexer #(.width(32)) multiplexer_12 (.in1({32{1'b0}}), .out(control_pc_1), .sel(halt));  // open: in0
  Multiplexer multiplexer_13 (.in1(1'b0), .out(wb_en_1), .sel(halt));  // open: in0
  Multiplexer #(.width(5)) multiplexer_14 (.in1({5{1'b0}}), .out(wb_addr_1), .sel(halt));  // open: in0
  Multiplexer #(.width(32)) multiplexer_15 (.in1({32{1'b0}}), .out(wb_data_1), .sel(halt));  // open: in0
  decode decode_1 (
    .opcode(inst[1:0]), .func3(inst[15:13]), .part5(inst[12]), .add(add), .lui(lui), .mv(mv), .swsp(swsp),
    .addi4spn(addi4spn), .sw(sw), .addi(addi), .beqz(beqz), .slli(slli), .j(j), .li(li), .lw(lw), .halt(halt));
  Multiplexer multiplexer_16 (.in1(instruc_li_1_wb_en), .out(wb_en_1), .sel(li));  // open: in0
  Multiplexer multiplexer_17 (.in1(instruc_lui_1_wb_en), .out(wb_en_1), .sel(lui));  // open: in0
  regfile regfile_1 (
    .clk(clk), .wb_en(wb_en), .wb_addr(wb_addr), .rs2(inst[6:2]), .wb_data(wb_data), .rs1(inst[11:7]),
    .x_rs1(x_rs1), .x_rs2(x_rs2));
  Multiplexer #(.width(5)) multiplexer_18 (.in1(instruc_li_1_rd), .out(wb_addr_1), .sel(li));  // open: in0
  Multiplexer #(.width(32)) multiplexer_19 (.in1(instruc_li_1_alu_result), .out(alu_result_1), .sel(li));  // open: in0
  Multiplexer #(.width(5)) multiplexer_20 (.in1(instruc_lui_1_rd), .out(wb_addr_1), .sel(lui));  // open: in0
  Multiplexer multiplexer_21 (.in1(instruc_li_1_mem_ren), .out(mem_ren_1), .sel(li));  // open: in0
  Multiplexer multiplexer_22 (.in1(instruc_lui_1_mem_ren), .out(mem_ren_1), .sel(lui));  // open: in0
  Multiplexer #(.width(32)) multiplexer_23 (
    .in1(instruc_lui_1_alu_result), .out(alu_result_1), .sel(lui));  // open: in0
  Register #(.width(1)) register_1 (.clk(clk), .Q(register_1_q), .clr(rst));  // open: D, en
  Register #(.width(1)) register_2 (.clk(clk), .Q(register_2_q), .clr(rst));  // open: D, en
  Register #(.width(1)) register_3 (.clk(clk), .Q(register_3_q), .clr(rst));  // open: D, en
  Register #(.width(1)) register_4 (.clk(clk), .Q(register_4_q), .clr(rst));  // open: D, en
  Register #(.width(5)) register_5 (.clk(clk), .Q(register_5_q), .clr(rst));  // open: D, en
  Register #(.width(32)) register_6 (.clk(clk), .Q(register_6_q), .clr(rst));  // open: D, en
  Multiplexer multiplexer_24 (.in0(mem_wen_1), .in1(register_1_q), .out(mem_wen), .sel(rst));
  Multiplexer multiplexer_25 (.in0(mem_ren_1), .in1(register_2_q), .out(mem_ren), .sel(rst));
  Multiplexer multiplexer_26 (.in0(control_en_1), .in1(register_3_q), .out(control_en), .sel(rst));
  Multiplexer multiplexer_27 (.in0(wb_en_1), .in1(register_4_q), .out(wb_en), .sel(rst));
  Multiplexer #(.width(5)) multiplexer_28 (.in0(wb_addr_1), .in1(register_5_q), .out(wb_addr), .sel(rst));
  Multiplexer #(.width(32)) multiplexer_29 (.in0(wb_data_1), .in1(register_6_q), .out(wb_data), .sel(rst));
  instruc_add instruc_add_1 (
    .clk(clk), .part3(inst[9:7]), .part4(inst[11:10]), .part1(inst[4:2]), .part2(inst[6:5]), .x_rs1(x_rs1),
    .x_rs2(x_rs2), .mem_wen(instruc_add_1_mem_wen), .mem_ren(instruc_add_1_mem_ren),
    .control_en(instruc_add_1_control_en), .wb_en(instruc_add_1_wb_en), .rd(instruc_add_1_rd),
    .wb_data(instruc_add_1_wb_data), .alu_result(instruc_add_1_alu_result));
  Multiplexer multiplexer_30 (.in1(instruc_add_1_mem_ren), .out(mem_ren_1), .sel(add));  // open: in0
  instruc_mv instruc_mv_1 (
    .clk(clk), .part3(inst[9:7]), .part4(inst[11:10]), .part1(inst[4:2]), .part2(inst[6:5]), .x_rs2(x_rs2),
    .mem_wen(instruc_mv_1_mem_wen), .mem_ren(instruc_mv_1_mem_ren), .control_en(instruc_mv_1_control_en),
    .wb_en(instruc_mv_1_wb_en), .rd(instruc_mv_1_rd), .wb_data(instruc_mv_1_wb_data),
    .alu_result(instruc_mv_1_alu_result));
  Multiplexer multiplexer_31 (.in1(instruc_mv_1_mem_ren), .out(mem_ren_1), .sel(mv));  // open: in0
  instruc_addi instruc_addi_1 (
    .clk(clk), .part3(inst[9:7]), .part4(inst[11:10]), .part1(inst[4:2]), .part2(inst[6:5]),
    .part5(inst[12]), .x_rs1(x_rs1), .mem_wen(instruc_addi_1_mem_wen), .mem_ren(instruc_addi_1_mem_ren),
    .control_en(instruc_addi_1_control_en), .wb_en(instruc_addi_1_wb_en), .rd(instruc_addi_1_rd),
    .wb_data(instruc_addi_1_wb_data), .alu_result(instruc_addi_1_alu_result));
  Multiplexer multiplexer_32 (.in1(instruc_addi_1_mem_ren), .out(mem_ren_1), .sel(addi));  // open: in0
  instruc_slli instruc_slli_1 (
    .clk(clk), .part3(inst[9:7]), .part4(inst[11:10]), .part1(inst[4:2]), .part2(inst[6:5]), .x_rs1(x_rs1),
    .mem_wen(instruc_slli_1_mem_wen), .mem_ren(instruc_slli_1_mem_ren),
    .control_en(instruc_slli_1_control_en), .wb_en(instruc_slli_1_wb_en), .rd(instruc_slli_1_rd),
    .wb_data(instruc_slli_1_wb_data), .alu_result(instruc_slli_1_alu_result));
  Register #(.width(32)) register_7 (.Q(register_7_q), .clr(rst));  // open: D, en, clk
  Multiplexer multiplexer_33 (.in1(instruc_add_1_mem_wen), .out(mem_wen_1), .sel(add));  // open: in0
  Multiplexer multiplexer_34 (.in1(instruc_mv_1_mem_wen), .out(mem_wen_1), .sel(mv));  // open: in0
  Multiplexer multiplexer_35 (.in1(instruc_addi_1_mem_wen), .out(mem_wen_1), .sel(addi));  // open: in0
  Multiplexer multiplexer_36 (.in1(instruc_slli_1_mem_ren), .out(mem_ren_1), .sel(slli));  // open: in0
  Register #(.width(32)) register_8 (.clk(clk), .Q(register_8_q), .clr(rst));  // open: D, en
  Multiplexer #(.width(32)) multiplexer_37 (
    .in1(instruc_add_1_alu_result), .out(alu_result_1), .sel(add));  // open: in0
  Multiplexer #(.width(32)) multiplexer_38 (.in1(instruc_mv_1_alu_result), .out(alu_result_1), .sel(mv));  // open: in0
  Multiplexer #(.width(32)) multiplexer_39 (
    .in1(instruc_addi_1_alu_result), .out(alu_result_1), .sel(addi));  // open: in0
  Multiplexer multiplexer_40 (.in1(instruc_slli_1_mem_wen), .out(mem_wen_1), .sel(slli));  // open: in0
  Multiplexer #(.width(32)) multiplexer_41 (
    .in1(instruc_slli_1_alu_result), .out(alu_result_1), .sel(slli));  // open: in0
  Multiplexer #(.width(32)) multiplexer_42 (.in0({32{1'b0}}), .in1(register_7_q), .out(mem_din), .sel(rst));
  Multiplexer #(.width(32)) multiplexer_43 (.in0({32{1'b0}}), .in1(register_7_q), .out(control_pc), .sel(rst));
  Multiplexer #(.width(32)) multiplexer_44 (.in0(alu_result_1), .in1(register_8_q), .out(alu_result), .sel(rst));
  Multiplexer multiplexer_45 (.in1(instruc_add_1_control_en), .out(control_en_1), .sel(add));  // open: in0
  Multiplexer #(.width(32)) multiplexer_46 (.in1(instruc_add_1_wb_data), .out(wb_data_1), .sel(add));  // open: in0
  Multiplexer multiplexer_47 (.in1(instruc_mv_1_control_en), .out(control_en_1), .sel(mv));  // open: in0
  Multiplexer #(.width(32)) multiplexer_48 (.in1(instruc_mv_1_wb_data), .out(wb_data_1), .sel(mv));  // open: in0
  Multiplexer multiplexer_49 (.in1(instruc_addi_1_control_en), .out(control_en_1), .sel(addi));  // open: in0
  Multiplexer #(.width(32)) multiplexer_50 (.in1(instruc_addi_1_wb_data), .out(wb_data_1), .sel(addi));  // open: in0
  Multiplexer multiplexer_51 (.in1(instruc_slli_1_control_en), .out(control_en_1), .sel(slli));  // open: in0
  Multiplexer #(.width(32)) multiplexer_52 (.in1(instruc_slli_1_wb_data), .out(wb_data_1), .sel(slli));  // open: in0
  Multiplexer multiplexer_53 (.in1(instruc_add_1_wb_en), .out(wb_en_1), .sel(add));  // open: in0
  Multiplexer multiplexer_54 (.in1(instruc_mv_1_wb_en), .out(wb_en_1), .sel(mv));  // open: in0
  Multiplexer multiplexer_55 (.in1(instruc_addi_1_wb_en), .out(wb_en_1), .sel(addi));  // open: in0
  Multiplexer multiplexer_56 (.in1(instruc_slli_1_wb_en), .out(wb_en_1), .sel(slli));  // open: in0
  Multiplexer #(.width(5)) multiplexer_57 (.in1(instruc_add_1_rd), .out(wb_addr_1), .sel(add));  // open: in0
  Multiplexer #(.width(5)) multiplexer_58 (.in1(instruc_mv_1_rd), .out(wb_addr_1), .sel(mv));  // open: in0
  Multiplexer #(.width(5)) multiplexer_59 (.in1(instruc_addi_1_rd), .out(wb_addr_1), .sel(addi));  // open: in0
  Multiplexer #(.width(5)) multiplexer_60 (.in1(instruc_slli_1_rd), .out(wb_addr_1), .sel(slli));  // open: in0

  // Other names for the same wires on the sheet: op[1:0] = inst[1:0]; part5 = inst[12]; func3[2:0] = inst[15:13];
  //   part3[2:0] = inst[9:7]; rs1[4:0] = inst[11:7]; part4[1:0] = inst[11:10]; part1[2:0] = inst[4:2];
  //   rs2[4:0] = inst[6:2]; part2[1:0] = inst[6:5]

  // Notes on the sheet:
  //   Fixed I/O
  //   Don't touch
endmodule

module testbench (
  input  rst,
  output mem_wen,
  output [31:0] mem_din,
  output mem_ren,
  output [31:0] alu_result,
  output control_en,
  output [31:0] control_pc,
  output halt,
  output wb_en,
  output [4:0] wb_addr,
  output [31:0] wb_data
);

  wire clk, inst_en, not_1_out, not_2_out, not_3_out, not_4_out, por_1_out, rst_t;
  wire [15:0] inst, inst_i;
  wire [31:0] current_pc, inst_addr, mem_result;

  not not_1 (not_1_out, inst_i[0]);
  not not_2 (not_2_out, inst_i[1]);
  not not_3 (not_3_out, inst_i[13]);
  not not_4 (not_4_out, inst_i[14]);
  and and_1 (halt, not_1_out, not_2_out, not_3_out, not_4_out, inst_i[15]);
  Clock clock_1 (.out(clk));
  or or_1 (rst_t, rst, por_1_out);
  POR por_1 (.out(por_1_out));
  inst_fetch inst_fetch_1 (
    .clk(clk), .rst(rst_t), .control_en_i(control_en), .control_pc_i(control_pc), .inst_i(inst_i),
    .inst_en_o(inst_en), .current_pc_o(current_pc), .inst_addr_o(inst_addr), .inst_o(inst));
  TOP top_1 (
    .rst(rst_t), .clk(clk), .inst(inst), .mem_result(mem_result), .current_pc(current_pc), .mem_wen(mem_wen),
    .mem_din(mem_din), .mem_ren(mem_ren), .alu_result(alu_result), .control_en(control_en),
    .control_pc(control_pc), .wb_en(wb_en), .wb_addr(wb_addr), .wb_data(wb_data));
  ROM #(.dataWidth(16)) rom_1 (.addr(inst_addr[7:0]), .data(inst_i));
  RAM #(.addrWidth(16), .clearpin("true"), .dataWidth(32), .\type ("nonvolatile")) ram_1 (
    .addr(alu_result[15:0]), .we(mem_wen), .oe(mem_ren), .clk(clk), .din(mem_din), .dout(mem_result),
    .clr(rst_t));

  // Notes on the sheet:
  //   contents of rom_1 (hex, n*v repeats v):
  //   4425 56fd 6525 7725 40e 972a 84a2 49d 16fd 8000
  //   you can write any instruction in
endmodule

module imm_gen (
  input  imm_5,
  input  [4:0] imm_4to0,
  input  ctrl,
  output [31:0] out_imm
);

  wire demultiplexer_1_out0, demultiplexer_1_out1;
  wire [11:0] bit_extender_3_out;
  wire [14:0] bit_extender_2_out;
  wire [26:0] bit_extender_1_out;

  Demultiplexer demultiplexer_1 (.out0(demultiplexer_1_out0), .out1(demultiplexer_1_out1), .in(imm_5), .sel(ctrl));
  assign bit_extender_1_out = {{26{demultiplexer_1_out0}}, demultiplexer_1_out0};  // Bit_Extender bit_extender_1
  assign bit_extender_2_out = {{14{demultiplexer_1_out1}}, demultiplexer_1_out1};  // Bit_Extender bit_extender_2
  assign bit_extender_3_out = {{11{1'b0}}, 1'b0};  // Bit_Extender bit_extender_3
  Multiplexer #(.width(32)) multiplexer_1 (
    .in0({bit_extender_1_out, imm_4to0}), .in1({bit_extender_2_out, imm_4to0, bit_extender_3_out}),
    .out(out_imm), .sel(ctrl));
endmodule

module decode (
  input  [1:0] opcode,
  input  [2:0] func3,
  input  part5,
  output add,
  output lui,
  output mv,
  output swsp,
  output addi4spn,
  output sw,
  output addi,
  output beqz,
  output slli,
  output j,
  output li,
  output lw,
  output halt
);

  wire CB, CI_2, CIW, comparator_4_eq, comparator_5_eq, comparator_6_eq, comparator_7_eq, comparator_8_eq,
       comparator_9_eq, comparator_10_eq, comparator_11_eq;

  Comparator #(.mode("unsigned"), .width(2)) comparator_1 (.a(opcode), .b(2'b01), .eq(CB));  // open: gt, lt
  Comparator #(.mode("unsigned"), .width(2)) comparator_2 (.a(opcode), .b(2'b10), .eq(CI_2));  // open: gt, lt
  Comparator #(.mode("unsigned"), .width(2)) comparator_3 (.a(opcode), .b(2'b00), .eq(CIW));  // open: gt, lt
  Comparator #(.mode("unsigned"), .width(4)) comparator_4 (
    .a({func3, part5}), .b(4'b1000), .eq(comparator_4_eq));  // open: gt, lt
  Comparator #(.mode("unsigned"), .width(4)) comparator_5 (
    .a({func3, part5}), .b(4'b1001), .eq(comparator_5_eq));  // open: gt, lt
  Comparator #(.mode("unsigned"), .width(3)) comparator_6 (
    .a(func3), .b(3'b000), .eq(comparator_6_eq));  // open: gt, lt
  Comparator #(.mode("unsigned"), .width(3)) comparator_7 (
    .a(func3), .b(3'b010), .eq(comparator_7_eq));  // open: gt, lt
  and and_1 (mv, comparator_4_eq, CI_2);
  and and_2 (add, comparator_5_eq, CI_2);
  and and_3 (addi4spn, CIW, comparator_6_eq);
  and and_4 (addi, CB, comparator_6_eq);
  and and_5 (slli, CI_2, comparator_6_eq);
  and and_6 (li, CB, comparator_7_eq);
  and and_7 (lw, comparator_7_eq, CIW);
  Comparator #(.mode("unsigned"), .width(3)) comparator_8 (
    .a(func3), .b(3'b011), .eq(comparator_8_eq));  // open: gt, lt
  Comparator #(.mode("unsigned"), .width(3)) comparator_9 (
    .a(func3), .b(3'b110), .eq(comparator_9_eq));  // open: gt, lt
  Comparator #(.mode("unsigned"), .width(3)) comparator_10 (
    .a(func3), .b(3'b101), .eq(comparator_10_eq));  // open: gt, lt
  Comparator #(.mode("unsigned"), .width(3)) comparator_11 (
    .a(func3), .b(3'b100), .eq(comparator_11_eq));  // open: gt, lt
  and and_8 (lui, comparator_8_eq, CB);
  and and_9 (swsp, CI_2, comparator_9_eq);
  and and_10 (sw, CIW, comparator_9_eq);
  and and_11 (beqz, CB, comparator_9_eq);
  and and_12 (j, comparator_10_eq, CB);
  and and_13 (halt, comparator_11_eq, CIW);

  // Other names for the same wires on the sheet: CI_1 = CB; CJ = CB; CR = CI_2; CSS = CI_2; CL = CIW; CS = CIW;
  //   halt_1 = CIW; op[1:0] = opcode
endmodule

module instruc_li (
  input  clk,
  input  [2:0] part3,
  input  [1:0] part4,
  input  part5,
  input  [2:0] part1,
  input  [1:0] part2,
  output mem_wen,
  output mem_ren,
  output control_en,
  output wb_en,
  output [4:0] rd,
  output [31:0] wb_data,
  output [31:0] alu_result
);

  imm_gen imm_gen_1 (.imm_5(part5), .imm_4to0({part2, part1}), .ctrl(1'b0), .out_imm(alu_result));

  assign control_en = 1'b0;
  assign mem_ren = 1'b0;
  assign mem_wen = 1'b0;
  assign rd = {part4, part3};
  assign wb_data = alu_result;
  assign wb_en = 1'b1;
endmodule

module instruc_lui (
  input  clk,
  input  [2:0] part3,
  input  [1:0] part4,
  input  part5,
  input  [2:0] part1,
  input  [1:0] part2,
  output mem_wen,
  output mem_ren,
  output control_en,
  output wb_en,
  output [4:0] rd,
  output [31:0] wb_data,
  output [31:0] alu_result
);

  imm_gen imm_gen_1 (.imm_5(part5), .imm_4to0({part2, part1}), .ctrl(1'b1), .out_imm(alu_result));

  assign control_en = 1'b0;
  assign mem_ren = 1'b0;
  assign mem_wen = 1'b0;
  assign rd = {part4, part3};
  assign wb_data = alu_result;
  assign wb_en = 1'b1;
endmodule

module instruc_add (
  input  clk,
  input  [2:0] part3,
  input  [1:0] part4,
  input  [2:0] part1,
  input  [1:0] part2,
  input  [31:0] x_rs1,
  input  [31:0] x_rs2,
  output mem_wen,
  output mem_ren,
  output control_en,
  output wb_en,
  output [4:0] rd,
  output [31:0] wb_data,
  output [31:0] alu_result
);

  Adder #(.width(32)) adder_1 (.a(x_rs1), .b(x_rs2), .out(alu_result));  // open: cin, cout

  assign control_en = 1'b0;
  assign mem_ren = 1'b0;
  assign mem_wen = 1'b0;
  assign rd = {part4, part3};
  assign wb_data = alu_result;
  assign wb_en = 1'b1;

  // Other names for the same wires on the sheet: rd_rs1[4:0] = {part4, part3}; result[31:0] = alu_result;
  //   rs2[4:0] = {part2, part1}
endmodule

module regfile (
  input  clk,
  input  wb_en,
  input  [4:0] wb_addr,
  input  [4:0] rs2,
  input  [31:0] wb_data,
  input  [4:0] rs1,
  output [31:0] x_rs1,
  output [31:0] x_rs2
);

  wire demultiplexer_1_out0, demultiplexer_1_out1, demultiplexer_1_out2, demultiplexer_1_out3,
       demultiplexer_1_out4, demultiplexer_1_out5, demultiplexer_1_out6, demultiplexer_1_out7;
  wire [31:0] register_1_q, register_2_q, register_3_q, register_4_q, register_5_q, register_6_q,
       register_7_q, register_8_q;

  Register #(.width(32)) register_1 (.D(wb_data), .en(demultiplexer_1_out0), .clk(clk), .Q(register_1_q));  // open: clr
  Register #(.width(32)) register_2 (.D(wb_data), .en(demultiplexer_1_out1), .clk(clk), .Q(register_2_q));  // open: clr
  Register #(.width(32)) register_3 (.D(wb_data), .en(demultiplexer_1_out2), .clk(clk), .Q(register_3_q));  // open: clr
  Register #(.width(32)) register_4 (.D(wb_data), .en(demultiplexer_1_out3), .clk(clk), .Q(register_4_q));  // open: clr
  Register #(.width(32)) register_5 (.D(wb_data), .en(demultiplexer_1_out4), .clk(clk), .Q(register_5_q));  // open: clr
  Demultiplexer #(.select(3)) demultiplexer_1 (
    .out0(demultiplexer_1_out0), .out1(demultiplexer_1_out1), .out2(demultiplexer_1_out2),
    .out3(demultiplexer_1_out3), .out4(demultiplexer_1_out4), .out5(demultiplexer_1_out5),
    .out6(demultiplexer_1_out6), .out7(demultiplexer_1_out7), .in(wb_en), .sel(wb_addr[2:0]));
  Register #(.width(32)) register_6 (.D(wb_data), .en(demultiplexer_1_out5), .clk(clk), .Q(register_6_q));  // open: clr
  Register #(.width(32)) register_7 (.D(wb_data), .en(demultiplexer_1_out6), .clk(clk), .Q(register_7_q));  // open: clr
  Register #(.width(32)) register_8 (.D(wb_data), .en(demultiplexer_1_out7), .clk(clk), .Q(register_8_q));  // open: clr
  Multiplexer #(.select(3), .width(32)) multiplexer_1 (
    .in0(register_1_q), .in1(register_2_q), .in2(register_3_q), .in3(register_4_q), .in4(register_5_q),
    .in5(register_6_q), .in6(register_7_q), .in7(register_8_q), .out(x_rs1), .sel(rs1[2:0]));
  Multiplexer #(.select(3), .width(32)) multiplexer_2 (
    .in0(register_1_q), .in1(register_2_q), .in2(register_3_q), .in3(register_4_q), .in4(register_5_q),
    .in5(register_6_q), .in6(register_7_q), .in7(register_8_q), .out(x_rs2), .sel(rs2[2:0]));

  // Other names for the same wires on the sheet: rs1_t[2:0] = rs1[2:0]; rs2_t[2:0] = rs2[2:0];
  //   wb_addr_t[2:0] = wb_addr[2:0]
endmodule

module instruc_mv (
  input  clk,
  input  [2:0] part3,
  input  [1:0] part4,
  input  [2:0] part1,
  input  [1:0] part2,
  input  [31:0] x_rs2,
  output mem_wen,
  output mem_ren,
  output control_en,
  output wb_en,
  output [4:0] rd,
  output [31:0] wb_data,
  output [31:0] alu_result
);


  assign alu_result = x_rs2;
  assign control_en = 1'b0;
  assign mem_ren = 1'b0;
  assign mem_wen = 1'b0;
  assign rd = {part4, part3};
  assign wb_data = x_rs2;
  assign wb_en = 1'b1;

  // Other names for the same wires on the sheet: rd_rs1[4:0] = {part4, part3}; result[31:0] = x_rs2;
  //   rs2[4:0] = {part2, part1}
endmodule

module instruc_addi (
  input  clk,
  input  [2:0] part3,
  input  [1:0] part4,
  input  [2:0] part1,
  input  [1:0] part2,
  input  part5,
  input  [31:0] x_rs1,
  output mem_wen,
  output mem_ren,
  output control_en,
  output wb_en,
  output [4:0] rd,
  output [31:0] wb_data,
  output [31:0] alu_result
);

  wire [31:0] imm_gen_1_out_imm;

  imm_gen imm_gen_1 (.imm_5(part5), .imm_4to0({part2, part1}), .ctrl(1'b0), .out_imm(imm_gen_1_out_imm));
  Adder #(.width(32)) adder_1 (.a(imm_gen_1_out_imm), .b(x_rs1), .out(alu_result));  // open: cin, cout

  assign control_en = 1'b0;
  assign mem_ren = 1'b0;
  assign mem_wen = 1'b0;
  assign rd = {part4, part3};
  assign wb_data = alu_result;
  assign wb_en = 1'b1;

  // Other names for the same wires on the sheet: imm_4to0[4:0] = {part2, part1}; rd_rs1[4:0] = {part4, part3}
endmodule

module instruc_slli (
  input  clk,
  input  [2:0] part3,
  input  [1:0] part4,
  input  [2:0] part1,
  input  [1:0] part2,
  input  [31:0] x_rs1,
  output mem_wen,
  output mem_ren,
  output control_en,
  output wb_en,
  output [4:0] rd,
  output [31:0] wb_data,
  output [31:0] alu_result
);

  Shifter #(.width(32)) shifter_1 (.in(x_rs1), .\dist ({part2, part1}), .out(alu_result));

  assign control_en = 1'b0;
  assign mem_ren = 1'b0;
  assign mem_wen = 1'b0;
  assign rd = {part4, part3};
  assign wb_data = alu_result;
  assign wb_en = 1'b1;

  // Other names for the same wires on the sheet: imm_4to0[4:0] = {part2, part1}; rd_rs1[4:0] = {part4, part3}
endmodule

module reset (
);

  wire control_en, rst;
  wire [4:0] wb_addr;
  wire [31:0] alu_result;

  Register #(.width(5)) register_1 (.Q(wb_addr), .clr(rst));  // open: D, en, clk
  Register #(.width(32)) register_2 (.Q(alu_result), .clr(rst));  // open: D, en, clk
  Register #(.width(1)) register_3 (.Q(control_en), .clr(rst));  // open: D, en, clk

  // Other names for the same wires on the sheet: control_pc[31:0] = alu_result; mem_din[31:0] = alu_result;
  //   wb_data[31:0] = alu_result; mem_ren = control_en; mem_wen = control_en; wb_en = control_en
endmodule
