// Logisim project proj_2_2.circ as structural Verilog: 19 circuits, main circuit testbench
module inst_fetch (
  input  clk,
  input  rst,
  input  control_en_i,
  input  [31:0] control_pc_i,
  input  [15:0] inst_i,
  output inst_en_o,
  output [31:0] current_pc_o,
  output [31:0] inst_addr_o,
  output [15:0] inst_o
);

  wire not_1_out, not_2_out;
  wire [31:0] adder_1_out, counter_1_q, multiplexer_1_out;

  not not_1 (not_1_out, rst);
  Adder #(.width(32)) adder_1 (.a(control_pc_i), .b(32'h1), .out(adder_1_out));  // open: cin, cout
  Counter #(.max('hffffffff), .width(32)) counter_1 (
    .clr(rst), .load(control_en_i), .up(not_1_out), .count(not_1_out), .clk(clk), .D(adder_1_out),
    .Q(counter_1_q));  // open: carry
  Multiplexer #(.width(32)) multiplexer_1 (
    .in0(counter_1_q), .in1(control_pc_i), .out(multiplexer_1_out), .sel(control_en_i));
  not not_2 (not_2_out, rst);
  Register #(.width(32)) register_1 (.D(multiplexer_1_out), .en(not_2_out), .clk(clk), .Q(current_pc_o), .clr(rst));
  not not_3 (inst_en_o, rst);

  assign inst_addr_o = current_pc_o;
  assign inst_o = inst_i;

  // Notes on the sheet:
  //   Don't touch
endmodule

module TOP (
  input  rst,
  input  clk,
  input  [15:0] inst,
  input  [31:0] mem_result,
  input  [31:0] current_pc,
  output mem_wen,
  output [31:0] mem_din,
  output mem_ren,
  output [31:0] alu_result,
  output control_en,
  output [31:0] control_pc,
  output wb_en,
  output [4:0] wb_addr,
  output [31:0] wb_data
);

  wire add, addi, addi4spn, and_1_out, and_2_out, beqz, control_en_1, halt, instruc_add_1_control_en,
       instruc_add_1_mem_ren, instruc_add_1_mem_wen, instruc_add_1_wb_en, instruc_addi4spn_1_control_en,
       instruc_addi4spn_1_mem_ren, instruc_addi4spn_1_mem_wen, instruc_addi4spn_1_wb_en,
       instruc_addi_1_control_en, instruc_addi_1_mem_ren, instruc_addi_1_mem_wen, instruc_addi_1_wb_en,
       instruc_beqz_1_control_en, instruc_beqz_1_mem_ren, instruc_beqz_1_mem_wen, instruc_beqz_1_wb_en,
       instruc_j_1_control_en, instruc_j_1_mem_ren, instruc_j_1_mem_wen, instruc_j_1_wb_en,
       instruc_jr_1_control_en, instruc_jr_1_mem_ren, instruc_jr_1_mem_wen, instruc_jr_1_wb_en,
       instruc_li_1_control_en, instruc_li_1_mem_ren, instruc_li_1_mem_wen, instruc_li_1_wb_en,
       instruc_lui_1_control_en, instruc_lui_1_mem_ren, instruc_lui_1_mem_wen, instruc_lui_1_wb_en,
       instruc_lw_1_control_en, instruc_lw_1_mem_ren, instruc_lw_1_mem_wen, instruc_lw_1_wb_en,
       instruc_mv_1_control_en, instruc_mv_1_mem_ren, instruc_mv_1_mem_wen, instruc_mv_1_wb_en,
       instruc_slli_1_control_en, instruc_slli_1_mem_ren, instruc_slli_1_mem_wen, instruc_slli_1_wb_en,
       instruc_sw_1_control_en, instruc_sw_1_mem_ren, instruc_sw_1_mem_wen, instruc_sw_1_wb_en,
       instruc_swsp_1_control_en, instruc_swsp_1_mem_ren, instruc_swsp_1_mem_wen, instruc_swsp_1_wb_en,
       is_jr, j, li, lui, lw, mem_ren_1, mem_wen_1, mv, not_1_out, or_1_out, slli, sw, swsp, wb_en_1;
  wire [4:0] instruc_add_1_rd, instruc_addi4spn_1_wb_addr, instruc_addi_1_rd, instruc_li_1_rd,
       instruc_lui_1_rd, instruc_lw_1_wb_addr, instruc_mv_1_rd, instruc_slli_1_rd, wb_addr_1;
  wire [4:3] rs1, rs2;
  wire [31:0] alu_result_1, control_pc_1, instruc_add_1_alu_result, instruc_add_1_wb_data,
       instruc_addi4spn_1_alu_result, instruc_addi4spn_1_wb_data, instruc_addi_1_alu_result,
       instruc_addi_1_wb_data, instruc_beqz_1_control_pc, instruc_j_1_control_pc, instruc_jr_1_control_pc,
       instruc_li_1_alu_result, instruc_li_1_wb_data, instruc_lui_1_alu_result, instruc_lui_1_wb_data,
       instruc_lw_1_alu_result, instruc_lw_1_wb_data, instruc_mv_1_alu_result, instruc_mv_1_wb_data,
       instruc_slli_1_alu_result, instruc_slli_1_wb_data, instruc_sw_1_alu_result, instruc_sw_1_mem_din,
       instruc_swsp_1_alu_result, instruc_swsp_1_mem_din, mem_din_1, wb_data_1, x_2, x_rs1, x_rs2;

  Multiplexer #(.width(2)) multiplexer_1 (.in0(inst[6:5]), .in1(2'b01), .out(rs2), .sel(sw));
  Comparator #(.mode("unsigned"), .width(5)) comparator_1 (
    .a({rs2, inst[4:2]}), .b({5{1'b0}}), .eq(is_jr));  // open: gt, lt
  instruc_li instruc_li_1 (
    .clk(clk), .part3(inst[9:7]), .part4(inst[11:10]), .part5(inst[12]), .part1(inst[4:2]),
    .part2(inst[6:5]), .mem_wen(instruc_li_1_mem_wen), .mem_ren(instruc_li_1_mem_ren),
    .control_en(instruc_li_1_control_en), .wb_en(instruc_li_1_wb_en), .rd(instruc_li_1_rd),
    .wb_data(instruc_li_1_wb_data), .alu_result(instruc_li_1_alu_result));
  instruc_lui instruc_lui_1 (
    .clk(clk), .part3(inst[9:7]), .part4(inst[11:10]), .part5(inst[12]), .part1(inst[4:2]),
    .part2(inst[6:5]), .mem_wen(instruc_lui_1_mem_wen), .mem_ren(instruc_lui_1_mem_ren),
    .control_en(instruc_lui_1_control_en), .wb_en(instruc_lui_1_wb_en), .rd(instruc_lui_1_rd),
    .wb_data(instruc_lui_1_wb_data), .alu_result(instruc_lui_1_alu_result));
  Multiplexer multiplexer_2 (.in1(instruc_li_1_mem_wen), .out(mem_wen_1), .sel(li));  // open: in0
  Multiplexer multiplexer_3 (.in1(instruc_li_1_control_en), .out(control_en_1), .sel(li));  // open: in0
  Multiplexer #(.width(32)) multiplexer_4 (.in1(instruc_li_1_wb_data), .out(wb_data_1), .sel(li));  // open: in0
  Multiplexer multiplexer_5 (.in1(instruc_lui_1_mem_wen), .out(mem_wen_1), .sel(lui));  // open: in0
  Multiplexer multiplexer_6 (.in1(instruc_lui_1_control_en), .out(control_en_1), .sel(lui));  // open: in0
  Multiplexer #(.width(32)) multiplexer_7 (.in1(instruc_lui_1_wb_data), .out(wb_data_1), .sel(lui));  // open: in0
  Multiplexer multiplexer_8 (.in1(1'b0), .out(mem_wen_1), .sel(halt));  // open: in0
  Multiplexer #(.width(32)) multiplexer_9 (.in1({32{1'b0}}), .out(mem_din_1), .sel(halt));  // open: in0
  Multiplexer multiplexer_10 (.in1(1'b0), .out(mem_ren_1), .sel(halt));  // open: in0
  Multiplexer #(.width(32)) multiplexer_11 (.in1({32{1'b0}}), .out(alu_result_1), .sel(halt));  // open: in0
  Multiplexer multiplexer_12 (.in1(1'b0), .out(control_en_1), .sel(halt));  // open: in0
  Multiplexer #(.width(32)) multiplexer_13 (.in1({32{1'b0}}), .out(control_pc_1), .sel(halt));  // open: in0
  Multiplexer multiplexer_14 (.in1(1'b0), .out(wb_en_1), .sel(halt));  // open: in0
  Multiplexer #(.width(5)) multiplexer_15 (.in1({5{1'b0}}), .out(wb_addr_1), .sel(halt));  // open: in0
  Multiplexer #(.width(32)) multiplexer_16 (.in1({32{1'b0}}), .out(wb_data_1), .sel(halt));  // open: in0
  or or_1 (or_1_out, lw, sw, beqz);
  decode decode_1 (
    .opcode(inst[1:0]), .func3(inst[15:13]), .part5(inst[12]), .add(add), .lui(lui), .mv(mv), .swsp(swsp),
    .addi4spn(addi4spn), .sw(sw), .addi(addi), .beqz(beqz), .slli(slli), .j(j), .li(li), .lw(lw), .halt(halt));
  Multiplexer #(.width(2)) multiplexer_17 (.in0(inst[11:10]), .in1(2'b01), .out(rs1), .sel(or_1_out));
  Multiplexer multiplexer_18 (.in1(instruc_li_1_wb_en), .out(wb_en_1), .sel(li));  // open: in0
  Multiplexer multiplexer_19 (.in1(instruc_lui_1_wb_en), .out(wb_en_1), .sel(lui));  // open: in0
  regfile regfile_1 (
    .clk(clk), .wb_en(wb_en), .wb_addr(wb_addr), .rs2({rs2, inst[4:2]}), .wb_data(wb_data),
    .rs1({rs1, inst[9:7]}), .x_rs1(x_rs1), .x_rs2(x_rs2), .x_2(x_2));
  Multiplexer #(.width(5)) multiplexer_20 (.in1(instruc_li_1_rd), .out(wb_addr_1), .sel(li));  // open: in0
  Multiplexer #(.width(32)) multiplexer_21 (.in1(instruc_li_1_alu_result), .out(alu_result_1), .sel(li));  // open: in0
  Multiplexer #(.width(5)) multiplexer_22 (.in1(instruc_lui_1_rd), .out(wb_addr_1), .sel(lui));  // open: in0
  Multiplexer multiplexer_23 (.in1(instruc_li_1_mem_ren), .out(mem_ren_1), .sel(li));  // open: in0
  Multiplexer multiplexer_24 (.in1(instruc_lui_1_mem_ren), .out(mem_ren_1), .sel(lui));  // open: in0
  Multiplexer #(.width(32)) multiplexer_25 (
    .in1(instruc_lui_1_alu_result), .out(alu_result_1), .sel(lui));  // open: in0
  Multiplexer multiplexer_26 (.in0(mem_wen_1), .in1(1'b0), .out(mem_wen), .sel(rst));
  Multiplexer multiplexer_27 (.in0(mem_ren_1), .in1(1'b0), .out(mem_ren), .sel(rst));
  Multiplexer multiplexer_28 (.in0(control_en_1), .in1(1'b0), .out(control_en), .sel(rst));
  Multiplexer multiplexer_29 (.in0(wb_en_1), .in1(1'b0), .out(wb_en), .sel(rst));
  Multiplexer #(.width(5)) multiplexer_30 (.in0(wb_addr_1), .in1({5{1'b0}}), .out(wb_addr), .sel(rst));
  Multiplexer #(.width(32)) multiplexer_31 (.in0(wb_data_1), .in1({32{1'b0}}), .out(wb_data), .sel(rst));
  instruc_jr instruc_jr_1 (
    .x_rs1(x_rs1), .mem_wen(instruc_jr_1_mem_wen), .mem_ren(instruc_jr_1_mem_ren),
    .control_en(instruc_jr_1_control_en), .control_pc(instruc_jr_1_control_pc), .wb_en(instruc_jr_1_wb_en));
  instruc_add instruc_add_1 (
    .clk(clk), .part3(inst[9:7]), .part4(inst[11:10]), .part1(inst[4:2]), .part2(inst[6:5]), .x_rs1(x_rs1),
    .x_rs2(x_rs2), .mem_wen(instruc_add_1_mem_wen), .mem_ren(instruc_add_1_mem_ren),
    .control_en(instruc_add_1_control_en), .wb_en(instruc_add_1_wb_en), .rd(instruc_add_1_rd),
    .wb_data(instruc_add_1_wb_data), .alu_result(instruc_add_1_alu_result));
  Multiplexer multiplexer_32 (.in1(instruc_add_1_mem_ren), .out(mem_ren_1), .sel(add));  // open: in0
  instruc_mv instruc_mv_1 (
    .clk(clk), .part3(inst[9:7]), .part4(inst[11:10]), .part1(inst[4:2]), .part2(inst[6:5]), .x_rs2(x_rs2),
    .mem_wen(instruc_mv_1_mem_wen), .mem_ren(instruc_mv_1_mem_ren), .control_en(instruc_mv_1_control_en),
    .wb_en(instruc_mv_1_wb_en), .rd(instruc_mv_1_rd), .wb_data(instruc_mv_1_wb_data),
    .alu_result(instruc_mv_1_alu_result));
  Multiplexer multiplexer_33 (.in1(instruc_mv_1_mem_ren), .out(mem_ren_1), .sel(and_1_out));  // open: in0
  instruc_addi instruc_addi_1 (
    .clk(clk), .part3(inst[9:7]), .part4(inst[11:10]), .part1(inst[4:2]), .part2(inst[6:5]),
    .part5(inst[12]), .x_rs1(x_rs1), .mem_wen(instruc_addi_1_mem_wen), .mem_ren(instruc_addi_1_mem_ren),
    .control_en(instruc_addi_1_control_en), .wb_en(instruc_addi_1_wb_en), .rd(instruc_addi_1_rd),
    .wb_data(instruc_addi_1_wb_data), .alu_result(instruc_addi_1_alu_result));
  Multiplexer multiplexer_34 (.in1(instruc_addi_1_mem_ren), .out(mem_ren_1), .sel(addi));  // open: in0
  instruc_slli instruc_slli_1 (
    .clk(clk), .part3(inst[9:7]), .part4(inst[11:10]), .part1(inst[4:2]), .part2(inst[6:5]), .x_rs1(x_rs1),
    .mem_wen(instruc_slli_1_mem_wen), .mem_ren(instruc_slli_1_mem_ren),
    .control_en(instruc_slli_1_control_en), .wb_en(instruc_slli_1_wb_en), .rd(instruc_slli_1_rd),
    .wb_data(instruc_slli_1_wb_data), .alu_result(instruc_slli_1_alu_result));
  instruc_swsp instruc_swsp_1 (
    .x_rs2(x_rs2), .part3(inst[9:7]), .part4(inst[11:10]), .part5(inst[12]), .x_2(x_2),
    .mem_wen(instruc_swsp_1_mem_wen), .mem_din(instruc_swsp_1_mem_din), .mem_ren(instruc_swsp_1_mem_ren),
    .alu_result(instruc_swsp_1_alu_result), .control_en(instruc_swsp_1_control_en),
    .wb_en(instruc_swsp_1_wb_en));
  instruc_addi4spn instruc_addi4spn_1 (
    .rd(inst[4:2]), .x_2(x_2), .part2(inst[6:5]), .part3(inst[9:7]), .part4(inst[11:10]), .part5(inst[12]),
    .mem_wen(instruc_addi4spn_1_mem_wen), .mem_ren(instruc_addi4spn_1_mem_ren),
    .alu_result(instruc_addi4spn_1_alu_result), .control_en(instruc_addi4spn_1_control_en),
    .wb_en(instruc_addi4spn_1_wb_en), .wb_addr(instruc_addi4spn_1_wb_addr),
    .wb_data(instruc_addi4spn_1_wb_data));
  instruc_lw instruc_lw_1 (
    .rd(inst[4:2]), .part2(inst[6:5]), .part4(inst[11:10]), .part5(inst[12]), .mem_result(mem_result),
    .x_rs1(x_rs1), .mem_wen(instruc_lw_1_mem_wen), .mem_ren(instruc_lw_1_mem_ren),
    .alu_result(instruc_lw_1_alu_result), .control_en(instruc_lw_1_control_en), .wb_en(instruc_lw_1_wb_en),
    .wb_addr(instruc_lw_1_wb_addr), .wb_data(instruc_lw_1_wb_data));
  instruc_sw instruc_sw_1 (
    .x_rs1(x_rs1), .x_rs2(x_rs2), .part2(inst[6:5]), .part4(inst[11:10]), .part5(inst[12]),
    .mem_wen(instruc_sw_1_mem_wen), .mem_din(instruc_sw_1_mem_din), .mem_ren(instruc_sw_1_mem_ren),
    .alu_result(instruc_sw_1_alu_result), .control_en(instruc_sw_1_control_en), .wb_en(instruc_sw_1_wb_en));
  instruc_beqz instruc_beqz_1 (
    .current_pc(current_pc), .x_rs1(x_rs1), .part1(inst[4:2]), .part2(inst[6:5]), .part4(inst[11:10]),
    .part5(inst[12]), .mem_wen(instruc_beqz_1_mem_wen), .mem_ren(instruc_beqz_1_mem_ren),
    .control_en(instruc_beqz_1_control_en), .control_pc(instruc_beqz_1_control_pc),
    .wb_en(instruc_beqz_1_wb_en));
  instruc_j instruc_j_1 (
    .current_pc(current_pc), .part1(inst[4:2]), .part2(inst[6:5]), .part3(inst[9:7]), .part4(inst[11:10]),
    .part5(inst[12]), .mem_wen(instruc_j_1_mem_wen), .mem_ren(instruc_j_1_mem_ren),
    .control_en(instruc_j_1_control_en), .control_pc(instruc_j_1_control_pc), .wb_en(instruc_j_1_wb_en));
  Multiplexer multiplexer_35 (.in1(instruc_jr_1_mem_wen), .out(mem_wen_1), .sel(and_2_out));  // open: in0
  Multiplexer multiplexer_36 (.in1(instruc_add_1_mem_wen), .out(mem_wen_1), .sel(add));  // open: in0
  Multiplexer multiplexer_37 (.in1(instruc_mv_1_mem_wen), .out(mem_wen_1), .sel(and_1_out));  // open: in0
  Multiplexer multiplexer_38 (.in1(instruc_addi_1_mem_wen), .out(mem_wen_1), .sel(addi));  // open: in0
  Multiplexer multiplexer_39 (.in1(instruc_slli_1_mem_ren), .out(mem_ren_1), .sel(slli));  // open: in0
  Multiplexer #(.width(32)) multiplexer_40 (.in1(instruc_swsp_1_mem_din), .out(mem_din_1), .sel(swsp));  // open: in0
  Multiplexer multiplexer_41 (.in1(instruc_addi4spn_1_mem_ren), .out(mem_ren_1), .sel(addi4spn));  // open: in0
  Multiplexer multiplexer_42 (.in1(instruc_lw_1_mem_wen), .out(mem_wen_1), .sel(lw));  // open: in0
  Multiplexer multiplexer_43 (.in1(instruc_sw_1_mem_wen), .out(mem_wen_1), .sel(sw));  // open: in0
  Multiplexer #(.width(32)) multiplexer_44 (.in1(instruc_sw_1_alu_result), .out(alu_result_1), .sel(sw));  // open: in0
  Multiplexer multiplexer_45 (.in1(instruc_beqz_1_mem_wen), .out(mem_wen_1), .sel(beqz));  // open: in0
  Multiplexer multiplexer_46 (.in1(instruc_beqz_1_wb_en), .out(wb_en_1), .sel(beqz));  // open: in0
  Multiplexer multiplexer_47 (.in1(instruc_j_1_mem_wen), .out(mem_wen_1), .sel(j));  // open: in0
  Multiplexer multiplexer_48 (.in1(instruc_j_1_wb_en), .out(wb_en_1), .sel(j));  // open: in0
  Multiplexer multiplexer_49 (.in1(instruc_jr_1_wb_en), .out(wb_en_1), .sel(and_2_out));  // open: in0
  Multiplexer #(.width(32)) multiplexer_50 (
    .in1(instruc_add_1_alu_result), .out(alu_result_1), .sel(add));  // open: in0
  Multiplexer #(.width(32)) multiplexer_51 (
    .in1(instruc_mv_1_alu_result), .out(alu_result_1), .sel(and_1_out));  // open: in0
  and and_1 (and_1_out, mv, not_1_out);
  not not_1 (not_1_out, is_jr);
  Multiplexer #(.width(32)) multiplexer_52 (
    .in1(instruc_addi_1_alu_result), .out(alu_result_1), .sel(addi));  // open: in0
  Multiplexer multiplexer_53 (.in1(instruc_slli_1_mem_wen), .out(mem_wen_1), .sel(slli));  // open: in0
  Multiplexer multiplexer_54 (.in1(instruc_swsp_1_mem_wen), .out(mem_wen_1), .sel(swsp));  // open: in0
  Multiplexer multiplexer_55 (.in1(instruc_addi4spn_1_mem_wen), .out(mem_wen_1), .sel(addi4spn));  // open: in0
  Multiplexer multiplexer_56 (.in1(instruc_lw_1_wb_en), .out(wb_en_1), .sel(lw));  // open: in0
  and and_2 (and_2_out, mv, is_jr);
  Multiplexer #(.width(32)) multiplexer_57 (
    .in1(instruc_slli_1_alu_result), .out(alu_result_1), .sel(slli));  // open: in0
  Multiplexer #(.width(32)) multiplexer_58 (
    .in1(instruc_addi4spn_1_alu_result), .out(alu_result_1), .sel(addi4spn));  // open: in0
  Multiplexer multiplexer_59 (.in1(instruc_lw_1_mem_ren), .out(mem_ren_1), .sel(lw));  // open: in0
  Multiplexer #(.width(32)) multiplexer_60 (.in1(instruc_sw_1_mem_din), .out(mem_din_1), .sel(sw));  // open: in0
  Multiplexer multiplexer_61 (.in1(instruc_beqz_1_mem_ren), .out(mem_ren_1), .sel(beqz));  // open: in0
  Multiplexer multiplexer_62 (.in1(instruc_j_1_mem_ren), .out(mem_ren_1), .sel(j));  // open: in0
  Multiplexer multiplexer_63 (.in1(instruc_jr_1_mem_ren), .out(mem_ren_1), .sel(and_2_out));  // open: in0
  Multiplexer #(.width(32)) multiplexer_64 (.in0(mem_din_1), .in1({32{1'b0}}), .out(mem_din), .sel(rst));
  Multiplexer #(.width(32)) multiplexer_65 (.in0(control_pc_1), .in1({32{1'b0}}), .out(control_pc), .sel(rst));
  Multiplexer #(.width(32)) multiplexer_66 (.in0(alu_result_1), .in1({32{1'b0}}), .out(alu_result), .sel(rst));
  Multiplexer multiplexer_67 (.in1(instruc_add_1_control_en), .out(control_en_1), .sel(add));  // open: in0
  Multiplexer #(.width(32)) multiplexer_68 (.in1(instruc_add_1_wb_data), .out(wb_data_1), .sel(add));  // open: in0
  Multiplexer multiplexer_69 (.in1(instruc_mv_1_control_en), .out(control_en_1), .sel(and_1_out));  // open: in0
  Multiplexer #(.width(32)) multiplexer_70 (.in1(instruc_mv_1_wb_data), .out(wb_data_1), .sel(and_1_out));  // open: in0
  Multiplexer multiplexer_71 (.in1(instruc_addi_1_control_en), .out(control_en_1), .sel(addi));  // open: in0
  Multiplexer #(.width(32)) multiplexer_72 (.in1(instruc_addi_1_wb_data), .out(wb_data_1), .sel(addi));  // open: in0
  Multiplexer multiplexer_73 (.in1(instruc_slli_1_control_en), .out(control_en_1), .sel(slli));  // open: in0
  Multiplexer multiplexer_74 (.in1(instruc_swsp_1_mem_ren), .out(mem_ren_1), .sel(swsp));  // open: in0
  Multiplexer multiplexer_75 (.in1(instruc_addi4spn_1_control_en), .out(control_en_1), .sel(addi4spn));  // open: in0
  Multiplexer #(.width(5)) multiplexer_76 (.in1(instruc_lw_1_wb_addr), .out(wb_addr_1), .sel(lw));  // open: in0
  Multiplexer multiplexer_77 (.in1(instruc_sw_1_control_en), .out(control_en_1), .sel(sw));  // open: in0
  Multiplexer #(.width(32)) multiplexer_78 (.in1(instruc_slli_1_wb_data), .out(wb_data_1), .sel(slli));  // open: in0
  Multiplexer multiplexer_79 (.in1(instruc_swsp_1_wb_en), .out(wb_en_1), .sel(swsp));  // open: in0
  Multiplexer #(.width(32)) multiplexer_80 (
    .in1(instruc_addi4spn_1_wb_data), .out(wb_data_1), .sel(addi4spn));  // open: in0
  Multiplexer multiplexer_81 (.in1(instruc_beqz_1_control_en), .out(control_en_1), .sel(beqz));  // open: in0
  Multiplexer multiplexer_82 (.in1(instruc_j_1_control_en), .out(control_en_1), .sel(j));  // open: in0
  Multiplexer multiplexer_83 (.in1(instruc_jr_1_control_en), .out(control_en_1), .sel(and_2_out));  // open: in0
  Multiplexer multiplexer_84 (.in1(instruc_add_1_wb_en), .out(wb_en_1), .sel(add));  // open: in0
  Multiplexer multiplexer_85 (.in1(instruc_mv_1_wb_en), .out(wb_en_1), .sel(and_1_out));  // open: in0
  Multiplexer multiplexer_86 (.in1(instruc_addi_1_wb_en), .out(wb_en_1), .sel(addi));  // open: in0
  Multiplexer multiplexer_87 (.in1(instruc_slli_1_wb_en), .out(wb_en_1), .sel(slli));  // open: in0
  Multiplexer #(.width(32)) multiplexer_88 (
    .in1(instruc_swsp_1_alu_result), .out(alu_result_1), .sel(swsp));  // open: in0
  Multiplexer #(.width(32)) multiplexer_89 (.in1(instruc_lw_1_wb_data), .out(wb_data_1), .sel(lw));  // open: in0
  Multiplexer multiplexer_90 (.in1(instruc_sw_1_mem_ren), .out(mem_ren_1), .sel(sw));  // open: in0
  Multiplexer multiplexer_91 (.in1(instruc_sw_1_wb_en), .out(wb_en_1), .sel(sw));  // open: in0
  Multiplexer multiplexer_92 (.in1(instruc_addi4spn_1_wb_en), .out(wb_en_1), .sel(addi4spn));  // open: in0
  Multiplexer #(.width(32)) multiplexer_93 (.in1(instruc_lw_1_alu_result), .out(alu_result_1), .sel(lw));  // open: in0
  Multiplexer #(.width(32)) multiplexer_94 (
    .in1(instruc_jr_1_control_pc), .out(control_pc_1), .sel(and_2_out));  // open: in0
  Multiplexer #(.width(5)) multiplexer_95 (.in1(instruc_add_1_rd), .out(wb_addr_1), .sel(add));  // open: in0
  Multiplexer #(.width(5)) multiplexer_96 (.in1(instruc_mv_1_rd), .out(wb_addr_1), .sel(and_1_out));  // open: in0
  Multiplexer #(.width(5)) multiplexer_97 (.in1(instruc_addi_1_rd), .out(wb_addr_1), .sel(addi));  // open: in0
  Multiplexer #(.width(5)) multiplexer_98 (.in1(instruc_slli_1_rd), .out(wb_addr_1), .sel(slli));  // open: in0
  Multiplexer multiplexer_99 (.in1(instruc_swsp_1_control_en), .out(control_en_1), .sel(swsp));  // open: in0
  Multiplexer #(.width(32)) multiplexer_100 (
    .in1(instruc_beqz_1_control_pc), .out(control_pc_1), .sel(beqz));  // open: in0
  Multiplexer #(.width(32)) multiplexer_101 (.in1(instruc_j_1_control_pc), .out(control_pc_1), .sel(j));  // open: in0
  Multiplexer #(.width(5)) multiplexer_102 (
    .in1(instruc_addi4spn_1_wb_addr), .out(wb_addr_1), .sel(addi4spn));  // open: in0
  Multiplexer multiplexer_103 (.in1(instruc_lw_1_control_en), .out(control_en_1), .sel(lw));  // open: in0

  // Other names for the same wires on the sheet: op[1:0] = inst[1:0]; part2[1:0] = inst[6:5];
  //   part4[1:0] = inst[11:10]; part5 = inst[12]; func3[2:0] = inst[15:13]; part3[2:0] = inst[9:7];
  //   rs1[2:0] = inst[9:7]; part1[2:0] = inst[4:2]; rs2[2:0] = inst[4:2]

  // Notes on the sheet:
  //   Fixed I/O
  //   Don't touch
endmodule

module testbench (
  input  rst,
  output mem_wen,
  output [31:0] mem_din,
  output mem_ren,
  output [31:0] alu_result,
  output control_en,
  output [31:0] control_pc,
  output halt,
  output wb_en,
  output [4:0] wb_addr,
  output [31:0] wb_data
);

  wire clk, inst_en, not_1_out, not_2_out, not_3_out, not_4_out, por_1_out, rst_t;
  wire [15:0] inst, inst_i;
  wire [31:0] current_pc, inst_addr, mem_result;

  not not_1 (not_1_out, inst_i[0]);
  not not_2 (not_2_out, inst_i[1]);
  not not_3 (not_3_out, inst_i[13]);
  not not_4 (not_4_out, inst_i[14]);
  and and_1 (halt, not_1_out, not_2_out, not_3_out, not_4_out, inst_i[15]);
  Clock clock_1 (.out(clk));
  or or_1 (rst_t, rst, por_1_out);
  POR por_1 (.out(por_1_out));
  inst_fetch inst_fetch_1 (
    .clk(clk), .rst(rst_t), .control_en_i(control_en), .control_pc_i(control_pc), .inst_i(inst_i),
    .inst_en_o(inst_en), .current_pc_o(current_pc), .inst_addr_o(inst_addr), .inst_o(inst));
  TOP top_1 (
    .rst(rst_t), .clk(clk), .inst(inst), .mem_result(mem_result), .current_pc(current_pc), .mem_wen(mem_wen),
    .mem_din(mem_din), .mem_ren(mem_ren), .alu_result(alu_result), .control_en(control_en),
    .control_pc(control_pc), .wb_en(wb_en), .wb_addr(wb_addr), .wb_data(wb_data));
  ROM #(.dataWidth(16)) rom_1 (.addr(inst_addr[7:0]), .data(inst_i));
  RAM #(.addrWidth(16), .clearpin("true"), .dataWidth(32), .\type ("nonvolatile")) ram_1 (
    .addr(alu_result[15:0]), .we(mem_wen), .oe(mem_ren), .clk(clk), .din(mem_din), .dout(mem_result),
    .clr(rst_t));

  // Notes on the sheet:
  //   contents of rom_1 (hex, n*v repeats v):
  //   4409 147d c011 bffd 1 1 4111 5429 c422 44b5 48 8482 8526 414c 511 c148 8000
  //   you can write any instruction in
endmodule

module imm_gen (
  input  imm_5,
  input  [4:0] imm_4to0,
  input  ctrl,
  output [31:0] out_imm
);

  wire demultiplexer_1_out0, demultiplexer_1_out1;
  wire [11:0] bit_extender_3_out;
  wire [14:0] bit_extender_2_out;
  wire [26:0] bit_extender_1_out;

  Demultiplexer demultiplexer_1 (.out0(demultiplexer_1_out0), .out1(demultiplexer_1_out1), .in(imm_5), .sel(ctrl));
  assign bit_extender_1_out = {{26{demultiplexer_1_out0}}, demultiplexer_1_out0};  // Bit_Extender bit_extender_1
  assign bit_extender_2_out = {{14{demultiplexer_1_out1}}, demultiplexer_1_out1};  // Bit_Extender bit_extender_2
  assign bit_extender_3_out = {{11{1'b0}}, 1'b0};  // Bit_Extender bit_extender_3
  Multiplexer #(.width(32)) multiplexer_1 (
    .in0({bit_extender_1_out, imm_4to0}), .in1({bit_extender_2_out, imm_4to0, bit_extender_3_out}),
    .out(out_imm), .sel(ctrl));
endmodule

module decode (
  input  [1:0] opcode,
  input  [2:0] func3,
  input  part5,
  output add,
  output lui,
  output mv,
  output swsp,
  output addi4spn,
  output sw,
  output addi,
  output beqz,
  output slli,
  output j,
  output li,
  output lw,
  output halt
);

  wire CB, CI_2, CIW, comparator_4_eq, comparator_5_eq, comparator_6_eq, comparator_7_eq, comparator_8_eq,
       comparator_9_eq, comparator_10_eq, comparator_11_eq;

  Comparator #(.mode("unsigned"), .width(2)) comparator_1 (.a(opcode), .b(2'b01), .eq(CB));  // open: gt, lt
  Comparator #(.mode("unsigned"), .width(2)) comparator_2 (.a(opcode), .b(2'b10), .eq(CI_2));  // open: gt, lt
  Comparator #(.mode("unsigned"), .width(2)) comparator_3 (.a(opcode), .b(2'b00), .eq(CIW));  // open: gt, lt
  Comparator #(.mode("unsigned"), .width(4)) comparator_4 (
    .a({func3, part5}), .b(4'b1000), .eq(comparator_4_eq));  // open: gt, lt
  Comparator #(.mode("unsigned"), .width(4)) comparator_5 (
    .a({func3, part5}), .b(4'b1001), .eq(comparator_5_eq));  // open: gt, lt
  Comparator #(.mode("unsigned"), .width(3)) comparator_6 (
    .a(func3), .b(3'b000), .eq(comparator_6_eq));  // open: gt, lt
  Comparator #(.mode("unsigned"), .width(3)) comparator_7 (
    .a(func3), .b(3'b010), .eq(comparator_7_eq));  // open: gt, lt
  and and_1 (mv, comparator_4_eq, CI_2);
  and and_2 (add, comparator_5_eq, CI_2);
  and and_3 (addi4spn, CIW, comparator_6_eq);
  and and_4 (addi, CB, comparator_6_eq);
  and and_5 (slli, CI_2, comparator_6_eq);
  and and_6 (li, CB, comparator_7_eq);
  and and_7 (lw, comparator_7_eq, CIW);
  Comparator #(.mode("unsigned"), .width(3)) comparator_8 (
    .a(func3), .b(3'b011), .eq(comparator_8_eq));  // open: gt, lt
  Comparator #(.mode("unsigned"), .width(3)) comparator_9 (
    .a(func3), .b(3'b110), .eq(comparator_9_eq));  // open: gt, lt
  Comparator #(.mode("unsigned"), .width(3)) comparator_10 (
    .a(func3), .b(3'b101), .eq(comparator_10_eq));  // open: gt, lt
  Comparator #(.mode("unsigned"), .width(3)) comparator_11 (
    .a(func3), .b(3'b100), .eq(comparator_11_eq));  // open: gt, lt
  and and_8 (lui, comparator_8_eq, CB);
  and and_9 (swsp, CI_2, comparator_9_eq);
  and and_10 (sw, CIW, comparator_9_eq);
  and and_11 (beqz, CB, comparator_9_eq);
  and and_12 (j, comparator_10_eq, CB);
  and and_13 (halt, comparator_11_eq, CIW);

  // Other names for the same wires on the sheet: CI_1 = CB; CJ = CB; CR = CI_2; CSS = CI_2; CL = CIW; CS = CIW;
  //   halt_1 = CIW; op[1:0] = opcode
endmodule

module instruc_li (
  input  clk,
  input  [2:0] part3,
  input  [1:0] part4,
  input  part5,
  input  [2:0] part1,
  input  [1:0] part2,
  output mem_wen,
  output mem_ren,
  output control_en,
  output wb_en,
  output [4:0] rd,
  output [31:0] wb_data,
  output [31:0] alu_result
);

  imm_gen imm_gen_1 (.imm_5(part5), .imm_4to0({part2, part1}), .ctrl(1'b0), .out_imm(alu_result));

  assign control_en = 1'b0;
  assign mem_ren = 1'b0;
  assign mem_wen = 1'b0;
  assign rd = {part4, part3};
  assign wb_data = alu_result;
  assign wb_en = 1'b1;
endmodule

module instruc_lui (
  input  clk,
  input  [2:0] part3,
  input  [1:0] part4,
  input  part5,
  input  [2:0] part1,
  input  [1:0] part2,
  output mem_wen,
  output mem_ren,
  output control_en,
  output wb_en,
  output [4:0] rd,
  output [31:0] wb_data,
  output [31:0] alu_result
);

  imm_gen imm_gen_1 (.imm_5(part5), .imm_4to0({part2, part1}), .ctrl(1'b1), .out_imm(alu_result));

  assign control_en = 1'b0;
  assign mem_ren = 1'b0;
  assign mem_wen = 1'b0;
  assign rd = {part4, part3};
  assign wb_data = alu_result;
  assign wb_en = 1'b1;
endmodule

module instruc_add (
  input  clk,
  input  [2:0] part3,
  input  [1:0] part4,
  input  [2:0] part1,
  input  [1:0] part2,
  input  [31:0] x_rs1,
  input  [31:0] x_rs2,
  output mem_wen,
  output mem_ren,
  output control_en,
  output wb_en,
  output [4:0] rd,
  output [31:0] wb_data,
  output [31:0] alu_result
);

  Adder #(.width(32)) adder_1 (.a(x_rs1), .b(x_rs2), .out(alu_result));  // open: cin, cout

  assign control_en = 1'b0;
  assign mem_ren = 1'b0;
  assign mem_wen = 1'b0;
  assign rd = {part4, part3};
  assign wb_data = alu_result;
  assign wb_en = 1'b1;

  // Other names for the same wires on the sheet: rd_rs1[4:0] = {part4, part3}; result[31:0] = alu_result;
  //   rs2[4:0] = {part2, part1}
endmodule

module regfile (
  input  clk,
  input  wb_en,
  input  [4:0] wb_addr,
  input  [4:0] rs2,
  input  [31:0] wb_data,
  input  [4:0] rs1,
  output [31:0] x_rs1,
  output [31:0] x_rs2,
  output [31:0] x_2
);

  wire demultiplexer_1_out2, demultiplexer_1_out8, demultiplexer_1_out9, demultiplexer_1_out10,
       demultiplexer_1_out11, demultiplexer_1_out12, demultiplexer_1_out13, demultiplexer_1_out14,
       demultiplexer_1_out15;
  wire [31:0] register_2_q, register_3_q, register_4_q, register_5_q, register_6_q, register_7_q,
       register_8_q, register_9_q;

  Register #(.width(32)) register_1 (.D(wb_data), .en(demultiplexer_1_out2), .clk(clk), .Q(x_2));  // open: clr
  Register #(.width(32)) register_2 (.D(wb_data), .en(demultiplexer_1_out8), .clk(clk), .Q(register_2_q));  // open: clr
  Register #(.width(32)) register_3 (.D(wb_data), .en(demultiplexer_1_out9), .clk(clk), .Q(register_3_q));  // open: clr
  Register #(.width(32)) register_4 (
    .D(wb_data), .en(demultiplexer_1_out10), .clk(clk), .Q(register_4_q));  // open: clr
  Register #(.width(32)) register_5 (
    .D(wb_data), .en(demultiplexer_1_out11), .clk(clk), .Q(register_5_q));  // open: clr
  Register #(.width(32)) register_6 (
    .D(wb_data), .en(demultiplexer_1_out12), .clk(clk), .Q(register_6_q));  // open: clr
  Demultiplexer #(.select(5)) demultiplexer_1 (
    .out2(demultiplexer_1_out2), .out8(demultiplexer_1_out8), .out9(demultiplexer_1_out9),
    .out10(demultiplexer_1_out10), .out11(demultiplexer_1_out11), .out12(demultiplexer_1_out12),
    .out13(demultiplexer_1_out13), .out14(demultiplexer_1_out14), .out15(demultiplexer_1_out15), .in(wb_en),
    .sel(wb_addr));  // open: out0, out1, out3, out4, out5, out6, out7, out16, out17, out18, out19, out20, out21, out22, out23, out24, out25, out26, out27, out28, out29, out30, out31
  Register #(.width(32)) register_7 (
    .D(wb_data), .en(demultiplexer_1_out13), .clk(clk), .Q(register_7_q));  // open: clr
  Register #(.width(32)) register_8 (
    .D(wb_data), .en(demultiplexer_1_out14), .clk(clk), .Q(register_8_q));  // open: clr
  Register #(.width(32)) register_9 (
    .D(wb_data), .en(demultiplexer_1_out15), .clk(clk), .Q(register_9_q));  // open: clr
  Multiplexer #(.select(5), .width(32)) multiplexer_1 (
    .in2(x_2), .in8(register_2_q), .in9(register_3_q), .in10(register_4_q), .in11(register_5_q),
    .in12(register_6_q), .in13(register_7_q), .in14(register_8_q), .in15(register_9_q), .out(x_rs1), .sel(rs1));  // open: in0, in1, in3, in4, in5, in6, in7, in16, in17, in18, in19, in20, in21, in22, in23, in24, in25, in26, in27, in28, in29, in30, in31
  Multiplexer #(.select(5), .width(32)) multiplexer_2 (
    .in0(x_2), .in8(register_2_q), .in9(register_3_q), .in10(register_4_q), .in11(register_5_q),
    .in12(register_6_q), .in13(register_7_q), .in14(register_8_q), .in15(register_9_q), .out(x_rs2), .sel(rs2));  // open: in1, in2, in3, in4, in5, in6, in7, in16, in17, in18, in19, in20, in21, in22, in23, in24, in25, in26, in27, in28, in29, in30, in31
endmodule

module instruc_mv (
  input  clk,
  input  [2:0] part3,
  input  [1:0] part4,
  input  [2:0] part1,
  input  [1:0] part2,
  input  [31:0] x_rs2,
  output mem_wen,
  output mem_ren,
  output control_en,
  output wb_en,
  output [4:0] rd,
  output [31:0] wb_data,
  output [31:0] alu_result
);


  assign alu_result = x_rs2;
  assign control_en = 1'b0;
  assign mem_ren = 1'b0;
  assign mem_wen = 1'b0;
  assign rd = {part4, part3};
  assign wb_data = x_rs2;
  assign wb_en = 1'b1;

  // Other names for the same wires on the sheet: rd_rs1[4:0] = {part4, part3}; result[31:0] = x_rs2;
  //   rs2[4:0] = {part2, part1}
endmodule

module instruc_addi (
  input  clk,
  input  [2:0] part3,
  input  [1:0] part4,
  input  [2:0] part1,
  input  [1:0] part2,
  input  part5,
  input  [31:0] x_rs1,
  output mem_wen,
  output mem_ren,
  output control_en,
  output wb_en,
  output [4:0] rd,
  output [31:0] wb_data,
  output [31:0] alu_result
);

  wire [31:0] imm_gen_1_out_imm;

  imm_gen imm_gen_1 (.imm_5(part5), .imm_4to0({part2, part1}), .ctrl(1'b0), .out_imm(imm_gen_1_out_imm));
  Adder #(.width(32)) adder_1 (.a(imm_gen_1_out_imm), .b(x_rs1), .out(alu_result));  // open: cin, cout

  assign control_en = 1'b0;
  assign mem_ren = 1'b0;
  assign mem_wen = 1'b0;
  assign rd = {part4, part3};
  assign wb_data = alu_result;
  assign wb_en = 1'b1;

  // Other names for the same wires on the sheet: imm_4to0[4:0] = {part2, part1}; rd_rs1[4:0] = {part4, part3}
endmodule

module instruc_slli (
  input  clk,
  input  [2:0] part3,
  input  [1:0] part4,
  input  [2:0] part1,
  input  [1:0] part2,
  input  [31:0] x_rs1,
  output mem_wen,
  output mem_ren,
  output control_en,
  output wb_en,
  output [4:0] rd,
  output [31:0] wb_data,
  output [31:0] alu_result
);

  Shifter #(.width(32)) shifter_1 (.in(x_rs1), .\dist ({part2, part1}), .out(alu_result));

  assign control_en = 1'b0;
  assign mem_ren = 1'b0;
  assign mem_wen = 1'b0;
  assign rd = {part4, part3};
  assign wb_data = alu_result;
  assign wb_en = 1'b1;

  // Other names for the same wires on the sheet: imm_4to0[4:0] = {part2, part1}; rd_rs1[4:0] = {part4, part3}
endmodule

module instruc_swsp (
  input  [31:0] x_rs2,
  input  [2:0] part3,
  input  [1:0] part4,
  input  part5,
  input  [31:0] x_2,
  output mem_wen,
  output [31:0] mem_din,
  output mem_ren,
  output [31:0] alu_result,
  output control_en,
  output wb_en
);

  Adder #(.width(32)) adder_1 (
    .a({{24{1'b0}}, part3[1:0], part5, part4, part3[2], 2'b00}), .b(x_2), .out(alu_result));  // open: cin, cout

  assign control_en = 1'b0;
  assign mem_din = x_rs2;
  assign mem_ren = 1'b0;
  assign mem_wen = 1'b1;
  assign wb_en = 1'b0;
endmodule

module instruc_addi4spn (
  input  [2:0] rd,
  input  [31:0] x_2,
  input  [1:0] part2,
  input  [2:0] part3,
  input  [1:0] part4,
  input  part5,
  output mem_wen,
  output mem_ren,
  output [31:0] alu_result,
  output control_en,
  output wb_en,
  output [4:0] wb_addr,
  output [31:0] wb_data
);

  Adder #(.width(32)) adder_1 (
    .a({{22{1'b0}}, part4[0], part3, part5, part4[1], part2[0], part2[1], 2'b00}), .b(x_2), .out(alu_result));  // open: cin, cout

  assign control_en = 1'b0;
  assign mem_ren = 1'b0;
  assign mem_wen = 1'b0;
  assign wb_addr = {2'b01, rd};
  assign wb_data = alu_result;
  assign wb_en = 1'b1;
endmodule

module instruc_lw (
  input  [2:0] rd,
  input  [1:0] part2,
  input  [1:0] part4,
  input  part5,
  input  [31:0] mem_result,
  input  [31:0] x_rs1,
  output mem_wen,
  output mem_ren,
  output [31:0] alu_result,
  output control_en,
  output wb_en,
  output [4:0] wb_addr,
  output [31:0] wb_data
);

  Adder #(.width(32)) adder_1 (
    .a({{25{1'b0}}, part2[0], part5, part4, part2[1], 2'b00}), .b(x_rs1), .out(alu_result));  // open: cin, cout

  assign control_en = 1'b0;
  assign mem_ren = 1'b1;
  assign mem_wen = 1'b0;
  assign wb_addr = {2'b01, rd};
  assign wb_data = mem_result;
  assign wb_en = 1'b1;
endmodule

module instruc_sw (
  input  [31:0] x_rs1,
  input  [31:0] x_rs2,
  input  [1:0] part2,
  input  [1:0] part4,
  input  part5,
  output mem_wen,
  output [31:0] mem_din,
  output mem_ren,
  output [31:0] alu_result,
  output control_en,
  output wb_en
);

  Adder #(.width(32)) adder_1 (
    .a({{25{1'b0}}, part2[0], part5, part4, part2[1], 2'b00}), .b(x_rs1), .out(alu_result));  // open: cin, cout

  assign control_en = 1'b0;
  assign mem_din = x_rs2;
  assign mem_ren = 1'b0;
  assign mem_wen = 1'b1;
  assign wb_en = 1'b0;
endmodule

module instruc_beqz (
  input  [31:0] current_pc,
  input  [31:0] x_rs1,
  input  [2:0] part1,
  input  [1:0] part2,
  input  [1:0] part4,
  input  part5,
  output mem_wen,
  output mem_ren,
  output control_en,
  output [31:0] control_pc,
  output wb_en
);

  wire [23:0] bit_extender_1_out;

  Comparator #(.mode("unsigned"), .width(32)) comparator_1 (
    .a(x_rs1), .b({32{1'b0}}), .eq(control_en));  // open: gt, lt
  assign bit_extender_1_out = {{23{part5}}, part5};  // Bit_Extender bit_extender_1
  Adder #(.width(32)) adder_1 (
    .a({bit_extender_1_out, part2, part1[0], part4, part1[2:1], 1'b0}), .b(current_pc), .out(control_pc));  // open: cin, cout

  assign mem_ren = 1'b0;
  assign mem_wen = 1'b0;
  assign wb_en = 1'b0;

  // Other names for the same wires on the sheet: is_zero = control_en; new_pc[31:0] = control_pc
endmodule

module instruc_j (
  input  [31:0] current_pc,
  input  [2:0] part1,
  input  [1:0] part2,
  input  [2:0] part3,
  input  [1:0] part4,
  input  part5,
  output mem_wen,
  output mem_ren,
  output control_en,
  output [31:0] control_pc,
  output wb_en
);

  wire [20:0] bit_extender_1_out;

  assign bit_extender_1_out = {{20{part5}}, part5};  // Bit_Extender bit_extender_1
  Adder #(.width(32)) adder_1 (
    .a({bit_extender_1_out, part3[1], part4[1], part3[2], part2[1], part3[0], part1[0], part4[0], part2[0], part1[2:1], 1'b0}),
    .b(current_pc), .out(control_pc));  // open: cin, cout

  assign control_en = 1'b1;
  assign mem_ren = 1'b0;
  assign mem_wen = 1'b0;
  assign wb_en = 1'b0;

  // Other names for the same wires on the sheet: new_pc[31:0] = control_pc
endmodule

module instruc_jr (
  input  [31:0] x_rs1,
  output mem_wen,
  output mem_ren,
  output control_en,
  output [31:0] control_pc,
  output wb_en
);


  assign control_en = 1'b1;
  assign control_pc = x_rs1;
  assign mem_ren = 1'b0;
  assign mem_wen = 1'b0;
  assign wb_en = 1'b0;

  // Other names for the same wires on the sheet: new_pc[31:0] = x_rs1
endmodule
